# Fritzing sketch slave (saved by Fritzing 0.9.3b)
circuit board: 8.46667cm x 5.64444cm
breadboards: 1

parts:
  Composant2 = Arduino Nano (Rev3.0)
  LED1 = LED - 5mm [color="Red (633nm)" package="5 mm [THT]"]
  LED2 = LED - 5mm [color="Green (570nm)" package="5 mm [THT]"]
  S1 = Pushbutton [package=THT]
  R1 = Rotary Potentiometer (Small) [maximum_resistance=100kΩ package=THT]
  R2 = Resistor [tolerance=±5% resistance=10k package=THT]

nets:
  N1: Composant2.GND, LED1.cathode, LED2.cathode, R2.Pin_0
  VIN: Composant2.D2, Composant2.D3, Composant2.D4, Composant2.D5, Composant2.VIN, Composant2.5V, S1.leg0, R1.wiper
  N2: Composant2.D8, S1.leg1, R2.Pin_1
  N3: Composant2.D9, LED2.anode
  N4: Composant2.D10, LED1.anode
  N5: Composant2.A0, R1.leg2

// code stored in the sketch: master.ino
# master
#include <wWire.h>

# web server
